# Fritzing sketch Pailleron (saved by Fritzing 0.9.3b)
circuit board: 8.46667cm x 5.64444cm

parts:
  Composant1 = Arduino Uno (Rev3) - ICSP
  M1 = DC Motor
  S3 = Toggle Switch [package=THT]
  Composant3 = Adafruit MAX4466 Electret Microphone Amplifier [part_number="Adafruit #1063"]
  R1 = Resistor [tolerance=±5% resistance=10k package=THT]
  Composant4 = Motor Driver 1A Dual TB6612FNG

nets:
  N1: Composant1.A0, Composant3.OUT
  VCC: Composant1.5V, S3.COM, Composant3.VCC, Composant4.B01, Composant4.VCC
  N2: Composant1.D8, Composant4.STBY
  N3: Composant1.D9_PWM, Composant4.AIN1
  N4: Composant1.D10_PWM/SS, Composant4.AIN2
  N5: Composant1.D11_PWM/MOSI, Composant4.PWMA
  GND: Composant1.GND, M1.pin_2, Composant3.GND, R1.Pin_0, Composant4.GND, Composant4.VM
  N6: Composant1.D3_PWM, S3.L2, R1.Pin_1
  N7: M1.pin_1, Composant4.A01

custom parts:
  Adafruit MAX4466 Electret Microphone Amplifier: Add an ear to your project with this well-designed electret microphone amplifier. This fully assembled and tested board comes with a 20-20KHz electret microphone soldered on. For the amplification, we use the Maxim MAX4466, an op-amp specifically designed for this delicate task! The amplifier has excellent power supply noise rejection, so this amplifier sounds really good and isn't nearly as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
